# Fritzing sketch ZOP 7_fritzing-shema (saved by Fritzing 0.9.3b)
breadboards: 1

parts:
  hc-sr1 = hc-sr04
  Part1 = Arduino Uno (Rev3)
  R3 = Trimmer Potentiometer [maximum_resistance=10kΩ package=THT]
  LCD1 = LCD screen
  R4 = Resistor [tolerance=±5% resistance=22 part_number=22ohm package="0603 [SMD]"]

nets:
  N1: hc-sr1.VCC, R4.Pin_1
  N2: hc-sr1.Trig, Part1.D13/SCK
  N3: hc-sr1.Echo, Part1.D12/MISO
  GND: hc-sr1.GND, Part1.GND, R3.leg2, LCD1.VSS, LCD1.LED-
  N4: Part1.D9_PWM, LCD1.E
  N5: Part1.D10_PWM/SS, LCD1.R/W
  N6: Part1.D11_PWM/MOSI, LCD1.RS
  N7: Part1.D2, LCD1.DB4
  N8: Part1.D3_PWM, LCD1.DB5
  N9: Part1.D4, LCD1.DB6
  N10: Part1.D5_PWM, LCD1.DB7
  5V: Part1.5V, R3.leg1, LCD1.VDD, LCD1.LED+, R4.Pin_0
  N11: R3.wiper, LCD1.V0
